# Fritzing sketch Casio SA-46 Keyboard (saved by Fritzing 0.9.3b)
breadboards: 1
perfboards: 1

parts:
  U1 = 74HC595 [package="DIP16 [THT]"]
  J1 = female pin header, 12 pins [form="♀ (female)"]
  R1 = Resistor [tolerance=±5% resistance=10k package=THT]
  R2 = Resistor [tolerance=±5% resistance=10k package=THT]
  R3 = Resistor [tolerance=±5% resistance=10k package=THT]
  R4 = Resistor [tolerance=±5% resistance=10k package=THT]
  J2 = female pin header, 12 pins [form="♀ (female)"]
  U2 = 74HC595 [package="DIP16 [THT]"]
  R5 = Resistor [tolerance=±5% resistance=10k package=THT]
  R6 = Resistor [tolerance=±5% resistance=10k package=THT]
  R7 = Resistor [tolerance=±5% resistance=10k package=THT]
  R8 = Resistor [tolerance=±5% resistance=10k package=THT]
  Part1 = Arduino Uno (Rev3)
  DIN1 = DIN-5 jack (MIDI) [package=THT]
  R9 = Resistor [tolerance=±5% resistance=220 package=THT]
  Part3 = Arduino Nano (Rev3.0)

nets (from the breadboard view):
  N1: U1.Q1, J1.pin6
  N2: U1.Q2, J1.pin7
  N3: U1.Q3, J1.pin8
  N4: U1.Q4, J1.pin9
  N5: U1.Q5, J1.pin10
  N6: U1.Q6, J1.pin11
  N7: U1.Q7, J1.pin12
  GND: U1.GND, U1.MR, U1.OE, R1.Pin_1, R2.Pin_1, R3.Pin_1, R4.Pin_1, Part1.GND
  N8: U1.SH_CP, Part1.D9_PWM
  N9: U1.ST_CP, Part1.D10_PWM/SS
  N10: U1.DS, Part1.D11_PWM/MOSI
  N11: U1.Q0, J1.pin5
  VCC: U1.VCC, Part1.5V
  N12: J1.pin1, R1.Pin_0, Part1.D2
  N13: J1.pin2, R2.Pin_0, Part1.D3_PWM
  N14: J1.pin3, R3.Pin_0, Part1.D4
  N15: J1.pin4, R4.Pin_0, Part1.D5_PWM
  N16: J2.pin1, R8.Pin_0, Part3.D4
  N17: J2.pin2, R6.Pin_0, Part3.D5
  N18: J2.pin3, R7.Pin_0, Part3.D6
  N19: J2.pin4, R5.Pin_0, Part3.D7
  N20: J2.pin5, U2.Q0
  N21: J2.pin6, U2.Q1
  N22: J2.pin7, U2.Q2
  N23: J2.pin8, U2.Q3
  N24: J2.pin9, U2.Q4
  N25: J2.pin10, U2.Q5
  N26: J2.pin11, U2.Q6
  N27: J2.pin12, U2.Q7
  N28: U2.SH_CP, Part3.D8
  N29: U2.ST_CP, Part3.D9
  N30: U2.DS, Part3.D10
  N31: U2.VCC, R9.Pin_0
  N32: R6.Pin_1, R7.Pin_1, R8.Pin_1
  N33: DIN1.5, R9.Pin_1
  N34: DIN1.2, Part3.GND
  N35: DIN1.4, Part3.D1/TX
