# Fritzing sketch CasioSA-46UNO (saved by Fritzing 0.9.2b)
perfboards: 1
breadboards: 1

parts:
  Part2 = Arduino Uno (Rev3)
  U2 = 74HC595 [package="DIP16 [THT]"]
  J2 = female pin header, 12 pins [form="♀ (female)"]
  R5 = Resistor [tolerance=±5% resistance=10k package=THT]
  R6 = Resistor [tolerance=±5% resistance=10k package=THT]
  R7 = Resistor [tolerance=±5% resistance=10k package=THT]
  R8 = Resistor [tolerance=±5% resistance=10k package=THT]
  Part3 = Arduino Uno (Rev3)
  J3 = female pin header, 12 pins [form="♀ (female)"]
  R10 = Resistor [tolerance=±5% resistance=10k package=THT]
  R11 = Resistor [tolerance=±5% resistance=10k package=THT]
  R12 = Resistor [tolerance=±5% resistance=10k package=THT]
  R13 = Resistor [tolerance=±5% resistance=10k package=THT]
  DIN2 = DIN-5 jack (MIDI) [package=THT]
  U3 = 74HC595 [package="DIP16 [THT]"]
  R14 = Resistor [tolerance=±5% resistance=220 package=THT]
  Power_plug1 = Power plug
  C1 = Electrolytic Capacitor [capacitance=10µF package="100 mil [THT, electrolytic]"]
  U4 = Voltage Regulator LDO [package=sc70]
  SJ1 = Solder Jumper [package=sj_2s]
  LED1 = LED - 5mm [color="Red (633nm)" package="5 mm [THT]"]
  R15 = Resistor [tolerance=±5% resistance=220 package=THT]
  C2 = Electrolytic Capacitor [capacitance=1µF package="100 mil [THT, electrolytic]"]
  C3 = Ceramic Capacitor [capacitance=100nF package="100 mil [THT, multilayer]"]

nets:
  N1: Part2.D9_PWM, U2.SH_CP
  N2: Part2.D10_PWM/SS, U2.ST_CP
  N3: Part2.D11_PWM/MOSI, U2.DS
  N4: Part2.D2, J2.pin1, R5.Pin_0
  N5: Part2.D3_PWM, J2.pin2, R6.Pin_0
  N6: Part2.D4, J2.pin3, R8.Pin_0
  N7: Part2.D5_PWM, J2.pin4, R7.Pin_0
  5V: Part2.5V, U2.VCC, SJ1.2, C2.+, C3.1
  GND: Part2.GND, U2.GND, U2.MR, U2.OE, R5.Pin_1, R6.Pin_1, R7.Pin_1, R8.Pin_1, Power_plug1.GND, C1.-, U4.GND, R15.Pin_0, C2.-, C3.0
  N8: U2.Q1, J2.pin6
  N9: U2.Q2, J2.pin7
  N10: U2.Q3, J2.pin8
  N11: U2.Q4, J2.pin9
  N12: U2.Q5, J2.pin10
  N13: U2.Q6, J2.pin11
  N14: U2.Q7, J2.pin12
  N15: U2.Q0, J2.pin5
  N16: Part3.D9_PWM, U3.SH_CP
  N17: Part3.D10_PWM/SS, U3.ST_CP
  GND_2: Part3.GND, U3.GND, U3.MR, U3.OE
  N18: Part3.D1/TX, DIN2.4
  N19: Part3.D2, J3.pin1, R12.Pin_0
  N20: Part3.D3_PWM, J3.pin2, R11.Pin_0
  N21: Part3.D4, J3.pin3, R13.Pin_0
  N22: Part3.D5_PWM, J3.pin4, R10.Pin_0
  N23: Part3.3V3, R14.Pin_1
  N24: J3.pin5, U3.VCC
  N25: J3.pin6, U3.Q1
  N26: J3.pin7, U3.Q2
  N27: J3.pin8, U3.Q3
  N28: J3.pin9, U3.Q4
  N29: J3.pin10, U3.Q5
  N30: J3.pin11, U3.Q6
  N31: J3.pin12, U3.Q7
  N32: R11.Pin_1, R12.Pin_1, R13.Pin_1
  N33: DIN2.5, R14.Pin_0
  N34: Power_plug1.VCC, C1.+, U4.IN, U4.EN
  N35: U4.OUT, SJ1.1, LED1.anode
  N36: LED1.cathode, R15.Pin_1
